# Fritzing sketch wiring (saved by Fritzing 0.9.2b)
breadboards: 1

parts:
  U1 = NodeMCU V1.0
  U2 = PCF8574 [package="DIP16 [THT]"]
  JP1 = Header 2 [package=r_sw_th]
  U3 = POT [package=alps_pot]
  S1 = Toggle Switch [package=THT]
  S2 = Toggle Switch [package=THT]
  Part1 = Adafruit_BMP280
  OLED1 = OLED 128x64 I2C Monochrome Display  # not connected
  VCC1 = Battery block 9V  # not connected
  R1 = Resistor [tolerance=±5% resistance=10k package="0603 [SMD]"]
  R2 = Resistor [tolerance=±5% resistance=10k package="0603 [SMD]"]
  R3 = Resistor [tolerance=±5% resistance=10k package="0603 [SMD]"]
  R4 = Resistor [tolerance=±5% resistance=10k package="0603 [SMD]"]

nets:
  N1: U1.D1, U2.SCL, Part1.SCK/SCL
  N2: U1.D2, U2.SDA, Part1.SDI/SDA
  3V3: U1.3V3, U2.VCC, U3.E, S1.COM, S2.COM, Part1.VIN
  GND: U1.GND, U2.GND, U3.A, Part1.GND, R1.Pin_1, R2.Pin_1, R3.Pin_1, R4.Pin_1
  N3: U1.D6, U2.INT
  N4: U1.Vin, JP1.2
  N5: U1.A0, U3.S
  N6: U2.P4, S1.L2, R3.Pin_0
  N7: U2.P5, S1.L1, R4.Pin_0
  N8: U2.P6, S2.L2, R2.Pin_0
  N9: U2.P7, S2.L1, R1.Pin_0

custom parts:
  NodeMCU V1.0: ESP8266 based NodeMCU
  Adafruit_BMP280: Bosch has stepped up their game with their new BMP280 sensor, an environmental sensor with temperature, barometric pressure that is the next generation upgrade to the BMP085/BMP180/BMP183. This sensor is great for all sorts of weather sensing and can even be used in both I2C and SPI! This precision sensor from Bosch is the best low-cost, precision sensing solution for measuring barometric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
